# Fritzing sketch Relays linked (skeelo-mac's conflicted copy 2014-06-10) (saved by Fritzing 0.6.3b)
breadboards: 1

parts:
  Arduino1 = Arduino
  R1 = Trimmer Potentiometer [maximum_resistance=250kΩ package=THT]
  S1 = Toggle Switch [package=THT]
  K1 = Relay [part_number=FRS1B-S package=THT]  # not connected
  LED1 = LED - 5mm [color="Red (633nm)" package="5 mm [THT]"]
  R2 = Resistor [tolerance=±5% resistance=1k package=THT]

nets:
  N1: Arduino1.GND, R1.leg1, S1.L1, LED1.anode
  N2: Arduino1.D10, S1.COM, R2.Pin_1
  N3: Arduino1.+5V, R1.leg2, S1.L2
  N4: Arduino1.A0, R1.wiper
  N5: LED1.cathode, R2.Pin_0
