# Fritzing sketch Relays linked (saved by Fritzing 0.6.3b)
breadboards: 1

parts:
  Arduino1 = Arduino
  R1 = Trimmer Potentiometer [maximum_resistance=250kΩ package=THT]
  S1 = Toggle Switch [package=THT]
  K1 = Relay [part_number=FRS1B-S package=THT]  # not connected

nets:
  N1: Arduino1.GND, R1.leg1, S1.L1
  N2: Arduino1.D10, S1.COM
  N3: Arduino1.+5V, R1.leg2, S1.L2
  N4: Arduino1.A0, R1.wiper
