# Fritzing sketch Ske - Arduino  for Sequence Relay - power supply & relays (saved by Fritzing 0.6.3b)
breadboards: 1

parts:
  IC2 = ULN2803A [package=THT]
  Part9 = Relay_T73
  Part10 = Relay_T73
  Part11 = Relay_T73
  Part12 = Relay_T73
  Part13 = Relay_T73
  Part14 = Relay_T73
  Part15 = Relay_T73
  Part16 = Relay_T73
  J3 = female pin header, 10 pins [form="♀ (female)"]

nets:
  N1: IC2.In_1, J3.pin10
  N2: IC2.In_2, J3.pin9
  N3: IC2.In_3, J3.pin8
  N4: IC2.In_4, J3.pin7
  N5: IC2.In_5, J3.pin6
  N6: IC2.In_6, J3.pin5
  N7: IC2.In_7, J3.pin4
  N8: IC2.In_8, J3.pin3
  N9: IC2.0V, J3.pin2
  N10: IC2.COM_-_Common, J3.pin1
  N11: IC2.Out_8, Part11.connector0
  N12: IC2.Out_7, Part14.connector0
  N13: IC2.Out_6, Part15.connector0
  N14: IC2.Out_5, Part10.connector0
  N15: IC2.Out_4, Part16.connector0
  N16: IC2.Out_3, Part9.connector0
  N17: IC2.Out_2, Part12.connector0
  N18: IC2.Out_1, Part13.connector0
