# Fritzing sketch Ske - Arduino  for Sequence Relay - with power supply & relays (saved by Fritzing 0.6.3b)
breadboards: 1

parts:
  U1 = Voltage Regulator - 5V [package="TO220 [THT]"]
  U2 = atmega168 [package="DIP28 [THT]"]
  G_RX_TX = female pin header, 3 pins [form="♀ (female)"]
  Analog_Input = female pin header, 5 pins [form="♀ (female)"]
  POWER_LED = female pin header, 2 pins [form="♀ (female)"]
  R3 = Resistor [tolerance=±10% resistance=10k package=THT]
  R4 = Trimmer Potentiometer [maximum_resistance=10kΩ package=THT]
  power = female pin header, 3 pins [form="♀ (female)"]
  Master/slave/bypass = female pin header, 4 pins [form="♀ (female)"]
  XTAL1 = Crystal [frequency="16 Mhz" package=THT]
  R1 = Resistor [tolerance=±5% resistance=1k package=THT]
  C3 = Ceramic Capacitor [capacitance=100nF package="200 mil [THT, multilayer]"]
  S1 = Pushbutton [package="[THT]"]
  C1 = Electrolytic Capacitor [capacitance=1µF package="100 mil [THT, electrolytic]"]
  C2 = Electrolytic Capacitor [capacitance=1µF package="100 mil [THT, electrolytic]"]
  C4 = Ceramic Capacitor [capacitance=100nF package="200 mil [THT, multilayer]"]
  IC1 = ULN2803A [package=THT]
  Part1 = Relay_T73
  Part2 = Relay_T73
  Part3 = Relay_T73
  Part7 = Relay_T73
  Part8 = Relay_T73
  J2 = female pin header, 10 pins [form="♀ (female)"]
  J3 = female pin header, 10 pins [form="♀ (female)"]

nets:
  N1: U1.input_voltage, C1.+
  N2: U1.output_voltage, U2.Pin_7, U2.Pin_20, U2.Pin_21, power.pin3, Master/slave/bypass.pin4, R1.Pin_0, C2.+
  N3: U2.Pin_1, R1.Pin_1, S1.Pin_1, S1.Pin_2
  N4: U2.Pin_2, G_RX_TX.pin2
  N5: U2.Pin_3, G_RX_TX.pin3
  N6: U2.Pin_4, power.pin2
  N7: U2.Pin_5, Master/slave/bypass.pin3
  N8: U2.Pin_6, Master/slave/bypass.pin2
  N9: U2.Pin_8, U2.Pin_22, R3.Pin_0, R4.leg2
  N10: U2.Pin_9, XTAL1.pin_0, C4.1
  N11: U2.Pin_10, XTAL1.pin_1, C3.0
  N12: U2.Pin_11, J3.pin10
  N13: U2.Pin_12, J3.pin9
  N14: U2.Pin_13, J3.pin8
  N15: U2.Pin_14, J3.pin7
  N16: U2.Pin_15, J3.pin6
  N17: U2.Pin_16, J3.pin5
  N18: U2.Pin_17, J3.pin4
  N19: U2.Pin_18, J3.pin3
  N20: U2.Pin_19, POWER_LED.pin1
  N21: U2.Pin_23, R4.wiper
  N22: U2.Pin_24, Analog_Input.pin1
  N23: U2.Pin_25, Analog_Input.pin2
  N24: U2.Pin_26, Analog_Input.pin3
  N25: U2.Pin_27, Analog_Input.pin4
  N26: U2.Pin_28, Analog_Input.pin5
  N27: G_RX_TX.pin1, power.pin1, Master/slave/bypass.pin1, C3.1, S1.Pin_3, S1.Pin_4, C1.-, C2.-, C4.0, J3.pin2
  N28: POWER_LED.pin2, R3.Pin_1
  N29: R4.leg1, J3.pin1
  N30: IC1.In_1, J2.pin10
  N31: IC1.In_2, J2.pin9
  N32: IC1.In_3, J2.pin8
  N33: IC1.In_4, J2.pin7
  N34: IC1.In_5, J2.pin6
  N35: IC1.In_6, J2.pin5
  N36: IC1.In_7, J2.pin4
  N37: IC1.In_8, J2.pin3
  N38: IC1.0V, J2.pin2
  N39: IC1.COM_-_Common, J2.pin1
  N40: IC1.Out_5, Part3.connector0
  N41: IC1.Out_4, Part2.connector0
  N42: IC1.Out_3, Part1.connector0
  N43: IC1.Out_2, Part7.connector0
  N44: IC1.Out_1, Part8.connector0

notes:
  This is a breadboard Arduino without an FTDI chip. You can program the chip with a USB-Serial breakout board, by using an external programmer or by programming the MCU in an Arduino board and then popping it into this circuit. The power source should be at least 7 VDC. Related example: http://itp.nyu.edu/physcomp/Tutorials/ArduinoBreadboard
