# Fritzing sketch Ske - Arduino  for Sequence Relay (saved by Fritzing 0.6.3b)
breadboards: 1

parts:
  C1 = Electrolytic Capacitor [package=THT]
  C2 = Electrolytic Capacitor [package=THT]
  U1 = Voltage Regulator - 5V [package="TO220 [THT]"]
  U2 = atmega168 [package="DIP28 [THT]"]
  R1 = 1k Ω Resistor [package=THT]
  C3 = Ceramic Disk Capacitor [package=THT]
  C4 = Ceramic Disk Capacitor [package=THT]
  XTAL1 = Crystal [package=THT]
  Power_plug1 = Power plug
  G_RX_TX = female pin header, 3 pins [form="♀ (female)"]
  G_w/Relays_1-4 = female pin header, 5 pins [form="♀ (female)"]
  VCC_w/Relays_8-5 = female pin header, 5 pins [form="♀ (female)"]
  S1 = Pushbutton [package=THT]
  Analog_Input = female pin header, 5 pins [form="♀ (female)"]
  POWER_LED = female pin header, 2 pins [form="♀ (female)"]
  R3 = Resistor [tolerance=±5% resistance=220 package=THT]
  R4 = Trimmer Potentiometer [maximum_resistance=10kΩ package=THT]
  power = female pin header, 3 pins [form="♀ (female)"]
  Master/slave/bypass = female pin header, 4 pins [form="♀ (female)"]

nets:
  GND: C1.-, C2.-, U1.GND, U2.Pin_8, U2.Pin_22, C3.pin_1, C4.pin_0, Power_plug1.GND, G_RX_TX.pin1, G_w/Relays_1-4.pin1, S1.Pin_3, S1.Pin_4, R3.Pin_0, R4.leg2, power.pin1, Master/slave/bypass.pin1
  N1: C1.+, U1.input_voltage, Power_plug1.VCC
  N2: C2.+, U1.output_voltage, U2.Pin_7, U2.Pin_20, U2.Pin_21, R1.Pin_0, VCC_w/Relays_8-5.pin5, R4.leg1, power.pin3, Master/slave/bypass.pin4
  N3: U2.Pin_1, R1.Pin_1, S1.Pin_1, S1.Pin_2
  N4: U2.Pin_2, G_RX_TX.pin2
  N5: U2.Pin_3, G_RX_TX.pin3
  N6: U2.Pin_4, power.pin2
  N7: U2.Pin_5, Master/slave/bypass.pin3
  N8: U2.Pin_6, Master/slave/bypass.pin2
  N9: U2.Pin_9, C4.pin_1, XTAL1.pin_0
  N10: U2.Pin_10, C3.pin_0, XTAL1.pin_1
  N11: U2.Pin_11, G_w/Relays_1-4.pin2
  N12: U2.Pin_12, G_w/Relays_1-4.pin3
  N13: U2.Pin_13, G_w/Relays_1-4.pin4
  N14: U2.Pin_14, G_w/Relays_1-4.pin5
  N15: U2.Pin_15, VCC_w/Relays_8-5.pin1
  N16: U2.Pin_16, VCC_w/Relays_8-5.pin2
  N17: U2.Pin_17, VCC_w/Relays_8-5.pin3
  N18: U2.Pin_18, VCC_w/Relays_8-5.pin4
  N19: U2.Pin_19, POWER_LED.pin1
  N20: U2.Pin_23, R4.wiper
  N21: U2.Pin_24, Analog_Input.pin1
  N22: U2.Pin_25, Analog_Input.pin2
  N23: U2.Pin_26, Analog_Input.pin3
  N24: U2.Pin_27, Analog_Input.pin4
  N25: U2.Pin_28, Analog_Input.pin5
  N26: POWER_LED.pin2, R3.Pin_1

notes:
  This is a breadboard Arduino without an FTDI chip. You can program the chip with a USB-Serial breakout board, by using an external programmer or by programming the MCU in an Arduino board and then popping it into this circuit. The power source should be at least 7 VDC. Related example: http://itp.nyu.edu/physcomp/Tutorials/ArduinoBreadboard
