# Fritzing sketch arduino relay pcb (saved by Fritzing 0.8.7b)
circuit board: 6.49111cm x 4.61366cm
breadboards: 1

parts:
  U1 = Voltage Regulator - 5V [package="TO220 [THT]"]
  Power_plug1 = Power plug
  G_RX_TX = female pin header, 3 pins [form="♀ (female)"]
  P_M_blank = female pin header, 3 pins [form="♀ (female)"]
  G_w/Relays_1-4 = female pin header, 5 pins [form="♀ (female)"]
  VCC_w/Relays_8-5 = female pin header, 5 pins [form="♀ (female)"]
  Analog_Input_5-1 = female pin header, 6 pins [form="♀ (female)"]
  part = Pushbutton [package=THT]  # not connected
  C3 = Ceramic Capacitor [capacitance=100nF package="200 mil [THT, multilayer]"]
  C4 = Ceramic Capacitor [capacitance=100nF package="200 mil [THT, multilayer]"]
  R1 = Resistor [tolerance=±5% resistance=1k package=THT]
  XTAL1 = Crystal [frequency="16 Mhz" package=THT]
  U2 = atmega168 [package=dip]
  C2 = Electrolytic Capacitor [capacitance=1µF package="100 mil [THT, electrolytic]"]
  S1 = Pushbutton [package="[THT]"]
  C1 = Electrolytic Capacitor [capacitance=1µF package="100 mil [THT, electrolytic]"]

nets:
  N1: U1.input_voltage, Power_plug1.VCC, C1.+
  GND: U1.GND, Power_plug1.GND, G_RX_TX.pin1, G_w/Relays_1-4.pin1, C3.1, C4.0, U2.GND, C2.-, S1.Pin_3, S1.Pin_4, C1.-
  N2: U1.output_voltage, VCC_w/Relays_8-5.pin5, R1.Pin_0, U2.VCC, U2.AVCC, U2.AREF, C2.+
  N3: G_RX_TX.pin2, U2.D0_(RX)
  N4: G_RX_TX.pin3, U2.D1_(TX)
  N5: P_M_blank.pin1, U2.D2
  N6: P_M_blank.pin2, U2.D3_(PWM)
  N7: P_M_blank.pin3, U2.D4
  N8: G_w/Relays_1-4.pin2, U2.D5_(PWM)
  N9: G_w/Relays_1-4.pin3, U2.D6_(PWM)
  N10: G_w/Relays_1-4.pin4, U2.D7
  N11: G_w/Relays_1-4.pin5, U2.D8
  N12: VCC_w/Relays_8-5.pin1, U2.D9_(PWM)
  N13: VCC_w/Relays_8-5.pin2, U2.D10_(PWM)
  N14: VCC_w/Relays_8-5.pin3, U2.D11_(PWM)
  N15: VCC_w/Relays_8-5.pin4, U2.D12
  N16: Analog_Input_5-1.pin1, U2.A0
  N17: Analog_Input_5-1.pin2, U2.A1
  N18: Analog_Input_5-1.pin3, U2.A2
  N19: Analog_Input_5-1.pin4, U2.A3
  N20: Analog_Input_5-1.pin5, U2.A4
  N21: Analog_Input_5-1.pin6, U2.A5
  N22: C3.0, XTAL1.pin_1, U2.XLAT2
  N23: C4.1, XTAL1.pin_0, U2.XLAT1
  N24: R1.Pin_1, U2.RESET, S1.Pin_1, S1.Pin_2

notes:
  This is a breadboard Arduino without an FTDI chip. You can program the chip with a USB-Serial breakout board, by using an external programmer or by programming the MCU in an Arduino board and then popping it into this circuit. The power source should be at least 7 VDC. Related example: http://itp.nyu.edu/physcomp/Tutorials/ArduinoBreadboard
